# Fritzing sketch TSFRL_master_module (saved by Fritzing 0.9.0b)
circuit board: 6.08472cm x 5.3848cm
circuit board: 9cm x 7cm
perfboards: 1

parts:
  Data = LED - 3mm [color="Yellow (595nm)" package="3 mm [THT]"]
  keyStart = Pushbutton [package="[THT]"]
  keyRight = Pushbutton [package="[THT]"]
  keyReset = Pushbutton [package="[THT]"]
  11_male_pins = male pin header, 11 pins [form="♂ (male)"]
  Error = LED - 3mm [color="Red (660nm)" package="3 mm [THT]"]
  Done = LED - 3mm [color="Green (570nm)" package="3 mm [THT]"]
  keyLeft = Pushbutton [package="[THT]"]
  keyDown = Pushbutton [package="[THT]"]
  Start = LED - 3mm [color="Blue (525nm)" package="3 mm [THT]"]
  keyUp = Pushbutton [package="[THT]"]
  keyUP = Pushbutton [package="[THT]"]
  R1 = Resistor [tolerance=±5% resistance=10k package=THT]
  R2 = Resistor [tolerance=±5% resistance=100k package=THT]
  C1 = Ceramic Capacitor [capacitance=100nF package="100 mil [THT, multilayer]"]
  IC1 = Hex Inverter Schmitt Trigger SN74HC14 [package="DIP (Dual Inline)"]
  keyLEFT = Pushbutton [package="[THT]"]
  R3 = Resistor [tolerance=±5% resistance=10k package=THT]
  R4 = Resistor [tolerance=±5% resistance=100k package=THT]
  C2 = Ceramic Capacitor [capacitance=100nF package="100 mil [THT, multilayer]"]
  keyRIGHT = Pushbutton [package="[THT]"]
  R5 = Resistor [tolerance=±5% resistance=10k package=THT]
  R6 = Resistor [tolerance=±5% resistance=100k package=THT]
  C3 = Ceramic Capacitor [capacitance=100nF package="100 mil [THT, multilayer]"]
  keyDOWN = Pushbutton [package="[THT]"]
  R7 = Resistor [tolerance=±5% resistance=10k package=THT]
  R8 = Resistor [tolerance=±5% resistance=100k package=THT]
  C4 = Ceramic Capacitor [capacitance=100nF package="100 mil [THT, multilayer]"]
  keySTART = Pushbutton [package="[THT]"]
  R9 = Resistor [tolerance=±5% resistance=10k package=THT]
  R10 = Resistor [tolerance=±5% resistance=100k package=THT]
  C5 = Ceramic Capacitor [capacitance=100nF package="100 mil [THT, multilayer]"]
  keySTOP/CANCEL = Pushbutton [package="[THT]"]
  11_male_pins1 = male pin header, 11 pins [form="♂ (male)"]

nets (from the schematic view):
  GND: Data.cathode, keyStart.Pin_1, keyStart.Pin_2, keyRight.Pin_1, keyRight.Pin_2, keyReset.Pin_1, keyReset.Pin_2, 11_male_pins.pin1, Error.cathode, Done.cathode, keyLeft.Pin_1, keyLeft.Pin_2, keyDown.Pin_1, keyDown.Pin_2, keyUp.Pin_1, keyUp.Pin_2, keyUP.Pin_3, C1.0, IC1.GND, keyLEFT.Pin_3, C2.0, keyRIGHT.Pin_3, C3.0, keyDOWN.Pin_3, C4.0, keySTART.Pin_3, C5.0, keySTOP/CANCEL.Pin_4, 11_male_pins1.pin1
  N1: Data.anode, 11_male_pins.pin8
  N2: keyStart.Pin_3, keyStart.Pin_4, 11_male_pins.pin4
  N3: keyRight.Pin_3, keyRight.Pin_4, 11_male_pins.pin6
  N4: keyReset.Pin_3, keyReset.Pin_4, 11_male_pins.pin2
  N5: 11_male_pins.pin3, keyDown.Pin_3, keyDown.Pin_4
  N6: 11_male_pins.pin5, keyLeft.Pin_3, keyLeft.Pin_4
  N7: 11_male_pins.pin7, keyUp.Pin_3, keyUp.Pin_4
  N8: 11_male_pins.pin9, Error.anode
  N9: 11_male_pins.pin10, Done.anode
  N10: 11_male_pins.pin11, Start.anode
  N11: keyUP.Pin_1, keyUP.Pin_2, R1.Pin_0, R2.Pin_0
  5V: R1.Pin_1, IC1.VCC, R3.Pin_1, R5.Pin_1, R7.Pin_1, R9.Pin_1, 11_male_pins1.pin2
  keyUP_in: R2.Pin_1, C1.1, IC1.1A
  keyUP_out: IC1.1Y
  keyLEFT_in: IC1.2A, R4.Pin_1, C2.1
  keyLEFT_out: IC1.2Y
  keySTART_out: IC1.4Y
  keySTART_in: IC1.4A, R10.Pin_1, C5.1
  keyDOWN_out: IC1.5Y
  keyDOWN_in: IC1.5A, R8.Pin_1, C4.1
  keyRIGHT_out: IC1.6Y
  keyRIGHT_in: IC1.6A, R6.Pin_1, C3.1
  N12: keyLEFT.Pin_1, keyLEFT.Pin_2, R3.Pin_0, R4.Pin_0
  N13: keyRIGHT.Pin_1, keyRIGHT.Pin_2, R5.Pin_0, R6.Pin_0
  N14: keyDOWN.Pin_1, keyDOWN.Pin_2, R7.Pin_0, R8.Pin_0
  N15: keySTART.Pin_1, keySTART.Pin_2, R9.Pin_0, R10.Pin_0
