# Fritzing sketch TSFRL_master_module_keys (saved by Fritzing 0.9.0b)
circuit board: 9cm x 7cm
perfboards: 1

parts:
  keyUP = Pushbutton [package="[THT]"]
  keySTART = Pushbutton [package="[THT]"]
  keyDOWN = Pushbutton [package="[THT]"]
  keyRIGHT = Pushbutton [package="[THT]"]
  keyLEFT = Pushbutton [package="[THT]"]
  R9 = Resistor [tolerance=±5% resistance=10k package=THT]
  R7 = Resistor [tolerance=±5% resistance=10k package=THT]
  R3 = Resistor [tolerance=±5% resistance=10k package=THT]
  R5 = Resistor [tolerance=±5% resistance=10k package=THT]
  R1 = Resistor [tolerance=±5% resistance=10k package=THT]
  R2 = Resistor [tolerance=±5% resistance=100k package=THT]
  R10 = Resistor [tolerance=±5% resistance=100k package=THT]
  R8 = Resistor [tolerance=±5% resistance=100k package=THT]
  R4 = Resistor [tolerance=±5% resistance=100k package=THT]
  R6 = Resistor [tolerance=±5% resistance=100k package=THT]
  C1 = Ceramic Capacitor [capacitance=100nF package="100 mil [THT, multilayer]"]
  C5 = Ceramic Capacitor [capacitance=100nF package="100 mil [THT, multilayer]"]
  C4 = Ceramic Capacitor [capacitance=100nF package="100 mil [THT, multilayer]"]
  C2 = Ceramic Capacitor [capacitance=100nF package="100 mil [THT, multilayer]"]
  C3 = Ceramic Capacitor [capacitance=100nF package="100 mil [THT, multilayer]"]
  keySTOP/CANCEL = Pushbutton [package="[THT]"]
  KEYS_pins = male pin header, 8 pins [form="♂ (male)"]

nets:
  N1: keyUP.Pin_1, keyUP.Pin_2, R1.Pin_0, R2.Pin_0
  GND: keyUP.Pin_3, keyUP.Pin_4, keySTART.Pin_3, keySTART.Pin_4, keyDOWN.Pin_3, keyDOWN.Pin_4, keyRIGHT.Pin_3, keyRIGHT.Pin_4, keyLEFT.Pin_3, keyLEFT.Pin_4, C1.0, C5.0, C4.0, C2.0, C3.0, keySTOP/CANCEL.Pin_3, keySTOP/CANCEL.Pin_4, KEYS_pins.pin1
  N2: keySTART.Pin_1, keySTART.Pin_2, R9.Pin_0, R10.Pin_0
  N3: keyDOWN.Pin_1, keyDOWN.Pin_2, R7.Pin_0, R8.Pin_0
  N4: keyRIGHT.Pin_1, keyRIGHT.Pin_2, R3.Pin_0, R4.Pin_0
  N5: keyLEFT.Pin_1, keyLEFT.Pin_2, R5.Pin_0, R6.Pin_0
  5V: R9.Pin_1, R7.Pin_1, R3.Pin_1, R5.Pin_1, R1.Pin_1, KEYS_pins.pin8
  N6: R2.Pin_1, C1.1, KEYS_pins.pin7
  N7: R10.Pin_1, C5.1, KEYS_pins.pin3
  N8: R8.Pin_1, C4.1, KEYS_pins.pin4
  N9: R4.Pin_1, C2.1, KEYS_pins.pin6
  N10: R6.Pin_1, C3.1, KEYS_pins.pin5
  N11: keySTOP/CANCEL.Pin_1, keySTOP/CANCEL.Pin_2, KEYS_pins.pin2

notes:
  8) +5v
  7) keyUP
  6) keyRIGHT
  5) keyLEFT
  4) keyDOWN
  3)keySTART
  2)keySTOP/CANCEL
  1)GND
  Test Stand For Radio Lamps, Test Stand For Radio Lamps project: keys module, 1.0
  GND
  keySTOP/CANCEL
  keySTART
  keyDOWN
  keyLEFT
  keyRIGHT
  keyUP
  VCC +5V
