# Fritzing sketch TSFRL_power_module_and_data_bus (saved by Fritzing 0.9.0b)

parts:
  IC1 = Voltage Regulator [package=to220-igo]
  C1 = Capacitor Polarized [package=cpol-radial-100uf-25v]
  R1 = Resistor [tolerance=±5% resistance=220 package=THT]
  POWER = LED - 3mm [color="Red (633nm)" package="3 mm [THT]"]
  DATA/POWER_pins_master = male pin header, 5 pins [form="♂ (male)"]
  C2 = Capacitor Polarized [package=cpol-radial-10uf-16v]
  DATA/POWER_pins_slave = male pin header, 5 pins [form="♂ (male)"]
  DATA/POWER_pins_slave_2 = male pin header, 5 pins [form="♂ (male)"]
  DATA/POWER_pins_slave_3 = male pin header, 5 pins [form="♂ (male)"]
  U1 = Transformer [package=transformer]
  D1 = Rectifier Diode [part_number=1N4001 package="300 mil [THT]"]
  ~220V = Screw terminal - 2 pins [package=THT]
  D2 = Rectifier Diode [part_number=1N4001 package="300 mil [THT]"]
  D3 = Rectifier Diode [part_number=1N4001 package="300 mil [THT]"]
  D4 = Rectifier Diode [part_number=1N4001 package="300 mil [THT]"]

nets:
  GND: IC1.GND, C1.-, POWER.cathode, DATA/POWER_pins_master.pin2, C2.-, DATA/POWER_pins_slave.pin2, DATA/POWER_pins_slave_2.pin2, DATA/POWER_pins_slave_3.pin2, D1.anode, D4.anode
  12V: IC1.IN, C1.+, D2.cathode, D3.cathode
  N1: IC1.OUT, R1.Pin_0, C2.+
  5V: R1.Pin_1, POWER.anode, DATA/POWER_pins_master.pin1, DATA/POWER_pins_slave.pin1, DATA/POWER_pins_slave_2.pin1, DATA/POWER_pins_slave_3.pin1
  N2: DATA/POWER_pins_master.pin3, DATA/POWER_pins_slave.pin3, DATA/POWER_pins_slave_2.pin3, DATA/POWER_pins_slave_3.pin3
  N3: DATA/POWER_pins_master.pin4, DATA/POWER_pins_slave.pin4, DATA/POWER_pins_slave_2.pin4, DATA/POWER_pins_slave_3.pin4
  N4: DATA/POWER_pins_master.pin5, DATA/POWER_pins_slave.pin5, DATA/POWER_pins_slave_2.pin5, DATA/POWER_pins_slave_3.pin5
  N5: U1.1, ~220V.pin2
  N6: U1.2, ~220V.pin1
  N7: U1.3, D3.anode, D4.cathode
  N8: U1.4, D1.cathode, D2.anode

notes:
  TSFRL_master_module_keys
  8) +5v
  7) keyUP
  6) keyRIGHT
  5) keyLEFT
  4) keyDOWN
  3)keySTART
  2)keySTOP/CANCEL
  1)GND
  GND
  VCC +5V
  CANCEL signal
  RS485_a
  RS485_b
  Test Stand For Radio Lamps, Test Stand For Radio Lamps project: power module and data bus, 1.0

custom parts:
  Capacitor Polarized: Capacitor Polarized cpol-radial-10uf-16v
