# Fritzing sketch TSFRL_slave_module (saved by Fritzing 0.9.0b)
circuit board: 9cm x 7cm
perfboards: 1

parts:
  DATA/POWER_pins = male pin header, 5 pins [form="♂ (male)"]
  DATA = LED - 3mm [color="Yellow (595nm)" package="3 mm [THT]"]
  ARDUINO_NANO = Arduino Nano (Rev3.0)
  R1 = Resistor [tolerance=±5% resistance=220 package=THT]
  U2 = DS75176BN [package=dil08]
  R6 = Resistor [tolerance=±5% resistance=10k package=THT]
  R7 = Resistor [tolerance=±5% resistance=10k package=THT]
  R8 = Resistor [tolerance=±5% resistance=10k package=THT]
  R10 = Resistor [tolerance=±5% resistance=10k package=THT]
  R2 = Resistor [tolerance=±5% resistance=220 package=THT]
  LED2 = LED - 3mm [color="Red (633nm)" package="3 mm [THT]"]
  R3 = Resistor [tolerance=±5% resistance=220 package=THT]
  LED3 = LED - 3mm [color="Red (633nm)" package="3 mm [THT]"]
  R4 = Resistor [tolerance=±5% resistance=220 package=THT]
  LED4 = LED - 3mm [color="Red (633nm)" package="3 mm [THT]"]
  R9 = Resistor [tolerance=±5% resistance=10k package=THT]
  Q1 = PNP-Transistor [part_number=BC557B package="TO92 [THT]"]
  Q2 = PNP-Transistor [part_number=BC557B package="TO92 [THT]"]
  Q3 = PNP-Transistor [part_number=BC557B package="TO92 [THT]"]
  Q4 = PNP-Transistor [part_number=BC557B package="TO92 [THT]"]
  Q5 = PNP-Transistor [part_number=BC557B package="TO92 [THT]"]
  J4 = male pin header, 1 pin [form="♂ (male)" part_number="Tube pin"]
  R5 = Resistor [tolerance=±5% resistance=10k package=THT]
  Q6 = PNP-Transistor [part_number=BC557B package="TO92 [THT]"]
  J5 = male pin header, 2 pins [form="♂ (male)"]
  J6 = male pin header, 2 pins [form="♂ (male)"]
  Voltage_pins = male pin header, 2 pins [form="♂ (male)"]
  R11 = Resistor [tolerance=±5% resistance=220 package=THT]
  LED5 = LED - 3mm [color="Red (633nm)" package="3 mm [THT]"]
  Measure = male pin header, 4 pins [form="♂ (male)"]

nets:
  GND: DATA/POWER_pins.pin1, DATA.cathode, ARDUINO_NANO.GND, U2.GND, LED2.cathode, LED3.cathode, LED4.cathode, LED5.cathode
  N1: DATA/POWER_pins.pin2, U2.DO/RI#5
  N2: DATA/POWER_pins.pin3, U2.DO/RI#6
  5V: DATA/POWER_pins.pin4, ARDUINO_NANO.5V, U2.VCC
  N3: DATA/POWER_pins.pin5, ARDUINO_NANO.RESET
  N4: DATA.anode, R1.Pin_1
  N5: ARDUINO_NANO.D2, R2.Pin_0
  N6: ARDUINO_NANO.D3, R3.Pin_0
  N7: ARDUINO_NANO.D4, R4.Pin_0
  N8: ARDUINO_NANO.D5, R5.Pin_0
  N9: ARDUINO_NANO.D6, R6.Pin_0
  N10: ARDUINO_NANO.D7, R7.Pin_0
  N11: ARDUINO_NANO.D8, R8.Pin_0
  N12: ARDUINO_NANO.D9, R9.Pin_0
  N13: ARDUINO_NANO.D10, R10.Pin_0
  N14: ARDUINO_NANO.D11/MOSI, U2.DI
  N15: ARDUINO_NANO.D12/MISO, U2.RO
  N16: ARDUINO_NANO.A7, R11.Pin_0
  N17: ARDUINO_NANO.A4, Measure.pin4
  N18: ARDUINO_NANO.A3, Measure.pin3
  N19: ARDUINO_NANO.A2, Measure.pin2
  N20: ARDUINO_NANO.A1, Measure.pin1
  N21: ARDUINO_NANO.D13/SCK, R1.Pin_0, U2.RE, U2.DE
  N22: R6.Pin_1, Q1.B
  N23: R7.Pin_1, Q2.B
  N24: R8.Pin_1, Q3.B
  N25: R10.Pin_1, Q5.B
  N26: R2.Pin_1, LED2.anode
  N27: R3.Pin_1, LED3.anode
  N28: R4.Pin_1, LED4.anode
  N29: R9.Pin_1, Q4.B
  N30: Q1.E, Q2.E, Q3.E, Q4.E, Q5.E, J4.pin1, Q6.E
  Voltage_1: Q1.C, Voltage_pins.pin1
  Voltage_2: Q2.C, J6.pin2
  Voltage_3: Q3.C, J6.pin1
  Voltage_4: Q4.C, J5.pin2
  Voltage_5: Q5.C, J5.pin1
  N31: R5.Pin_1, Q6.B
  Voltage_0(negative): Q6.C, Voltage_pins.pin2
  N32: R11.Pin_1, LED5.anode

notes:
  GND
  VCC +5V
  RESET signal
  RS485_a
  RS485_b
  Test Stand For Radio Lamps, Test Stand For Radio Lamps project: slave module, 1.0
  DATA/POWER_pins
  1) RESET signal
  2) +5v
  3) RS485_a
  4) RS485_b
  5) GND

custom parts:
  DS75176BN: RS-485 transceiver
