# Fritzing sketch TSFVT_power_module_and_data_bus (saved by Fritzing 0.9.0b)
circuit board: 9cm x 7cm
perfboards: 1

parts:
  7805 = Voltage Regulator [package=to220-igo]
  C1 = Capacitor Polarized [part_number="100uf 25v" package=cpol-radial-100uf-25v]
  R1 = Resistor [tolerance=±5% resistance=220 package=THT]
  POWER = LED - 3mm [color="Red (633nm)" package="3 mm [THT]"]
  DATA/POWER_pins_master = male pin header, 5 pins [form="♂ (male)"]
  C2 = Capacitor Polarized [part_number="10uf 16v" package=cpol-radial-10uf-16v]
  DATA/POWER_pins_slave = male pin header, 5 pins [form="♂ (male)"]
  DATA/POWER_pins_slave_2 = male pin header, 5 pins [form="♂ (male)"]
  DATA/POWER_pins_slave_3 = male pin header, 5 pins [form="♂ (male)"]
  U1 = Transformer [package=transformer]
  D1 = Rectifier Diode [part_number=1N4001 package="300 mil [THT]"]
  ~220V = Screw terminal - 2 pins [package=THT]
  D2 = Rectifier Diode [part_number=1N4001 package="300 mil [THT]"]
  D3 = Rectifier Diode [part_number=1N4001 package="300 mil [THT]"]
  D4 = Rectifier Diode [part_number=1N4001 package="300 mil [THT]"]
  GND = male pin header, 1 pin [form="♂ (male)"]

nets:
  GND: 7805.GND, C1.-, POWER.cathode, DATA/POWER_pins_master.pin1, C2.-, DATA/POWER_pins_slave.pin1, DATA/POWER_pins_slave_2.pin1, DATA/POWER_pins_slave_3.pin1, D1.anode, D4.anode, GND.pin1
  12V: 7805.IN, C1.+, D2.cathode, D3.cathode
  5V: 7805.OUT, R1.Pin_0, DATA/POWER_pins_master.pin4, C2.+, DATA/POWER_pins_slave.pin4, DATA/POWER_pins_slave_2.pin4, DATA/POWER_pins_slave_3.pin4
  N1: R1.Pin_1, POWER.anode
  N2: DATA/POWER_pins_master.pin2, DATA/POWER_pins_slave.pin2, DATA/POWER_pins_slave_2.pin2, DATA/POWER_pins_slave_3.pin2
  N3: DATA/POWER_pins_master.pin3, DATA/POWER_pins_slave.pin3, DATA/POWER_pins_slave_2.pin3, DATA/POWER_pins_slave_3.pin3
  N4: DATA/POWER_pins_master.pin5, DATA/POWER_pins_slave.pin5, DATA/POWER_pins_slave_2.pin5, DATA/POWER_pins_slave_3.pin5
  N5: U1.1, ~220V.pin2
  N6: U1.2, ~220V.pin1
  N7: U1.3, D3.anode, D4.cathode
  N8: U1.4, D1.cathode, D2.anode

notes:
  DATA/POWER_pins
  1) RESET signal
  2) +5v
  3) RS485_a
  4) RS485_b
  5) GND
  RS485_b
  GND
  RESET signal
  RS485_a
  VCC +5V
  Test Stand For Vacuum Tube, Test Stand For Vacuum Tube project: power module and data bus, 1.0

custom parts:
  Capacitor Polarized: Capacitor Polarized cpol-radial-10uf-16v
